# Fritzing sketch master_casque_velo (saved by Fritzing 0.9.3b)
perfboards: 1

parts:
  C1 = Ceramic Capacitor [capacitance=100nF package="100 mil [THT, multilayer]"]
  LED1 = LED - 3mm [color="Red (633nm)" package="3 mm [THT]"]
  J1 = Piezo Speaker
  Composant1 = Adafruit MicroSD card breakout board [part_number="Adafruit #254"]
  Composant2 = Adafruit ICM20948
  J2 = Camdenboss CTB0158-4 [part_number=CTB0158-4 package=THT]
  A1 = ESP32 Wroom 32E dev board
  R1 = Resistor [tolerance=±5% resistance=220 package=THT]
  S1 = Pushbutton [package="[THT]"]

nets:
  N1: C1.1, Composant1.+3V3, J2.pin3, A1.Pin_1
  N2: LED1.cathode, R1.Pin_1
  GND: LED1.anode, J1.pin1, Composant1.GND, Composant2.GND, J2.pin4, A1.Pin_14, A1.Pin_32, A1.Pin_38, S1.Pin_1, S1.Pin_2
  N3: J1.pin2, A1.Pin_24
  N4: Composant1.CLK, A1.Pin_30
  N5: Composant1.DO, A1.Pin_31
  N6: Composant1.DI, A1.Pin_37
  N7: Composant1.CS, A1.Pin_29
  N8: Composant2.SDI/SDA, A1.Pin_33
  N9: Composant2.SCK/SCL, A1.Pin_36
  N10: Composant2.INT, A1.Pin_23
  N11: J2.pin2, A1.Pin_9
  N12: A1.Pin_7, S1.Pin_3, S1.Pin_4
  N13: A1.Pin_8, R1.Pin_0

custom parts:
  Adafruit MicroSD card breakout board: Not just a simple breakout board, this microSD adapter goes the extra mile - designed for ease of use. Onboard 5v->3v regulator provides 150mA for power-hungry cards 3v level shifting means you can use this with ease on either 3v or 5v systems Uses a proper level shifting chip, not resistors: less problems, and faster read/write access Use 3 or 4 digital pins to read and write 2Gb+ of storage!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
  ESP32 Wroom 32E dev board: The ESP32 WROOM-32E is a versatile and powerful module built around Espressif’s ESP32 chipset. It offers dual-core processing, integrated Wi-Fi and Bluetooth connectivity, and boasts a wide range of peripheral interfaces.
