# Fritzing sketch slave_casque_velo (saved by Fritzing 0.9.3b)
perfboards: 1

parts:
  A1 = ESP32 Wroom 32E dev board
  Composant1 = Adafruit ICM20948

nets:
  N1: A1.Pin_1, Composant1.VIN
  N2: A1.Pin_14, A1.Pin_32, A1.Pin_38, Composant1.GND
  N3: A1.Pin_31, Composant1.INT
  N4: A1.Pin_33, Composant1.SDI/SDA
  N5: A1.Pin_36, Composant1.SCK/SCL

custom parts:
  ESP32 Wroom 32E dev board: The ESP32 WROOM-32E is a versatile and powerful module built around Espressif’s ESP32 chipset. It offers dual-core processing, integrated Wi-Fi and Bluetooth connectivity, and boasts a wide range of peripheral interfaces.
